# Fritzing sketch Thermometer-Sketch (saved by Fritzing 1.0.1rc)
breadboards: 1

parts:
  WeMos_D1_Mini1 = WeMos D1 Mini
  DS1 = DS18B20 1-Wire Temperature Sensor [part_number=DS18B20]
  R1 = Resistor [tolerance=±5% resistance=4.7 package="2512 [SMD]"]

nets:
  5V: WeMos_D1_Mini1.5V, DS1.VDD
  N1: WeMos_D1_Mini1.D2, DS1.DQ
  N2: WeMos_D1_Mini1.G, DS1.GND, R1.Pin_0
